# Fritzing sketch WonderDevice ESP8266 2 temp and dist and counter (saved by Fritzing 0.9.3b)
breadboards: 1

parts:
  U1 = NodeMCU V1.0
  R2 = Resistor [tolerance=±5% resistance=4.7k package=THT]
  R4 = Resistor [tolerance=±1% resistance=6.0k package=THT]
  hc-sr1 = hc-sr04
  DS1 = DS18B20 1-Wire Temperature Sensor [part_number=DS18B20]
  DS2 = DS18B20 1-Wire Temperature Sensor [part_number=DS18B20]
  R5 = Resistor [tolerance=±5% resistance=4.7k package=THT]

nets:
  N1: U1.D1, hc-sr1.Trig
  N2: U1.D2, R4.Pin_1, R5.Pin_0
  N3: U1.D4, R2.Pin_0, DS1.VDD, DS2.DQ
  3V3: U1.3V3, R2.Pin_1, DS1.DQ, DS2.VDD
  GND: U1.GND, R4.Pin_0, hc-sr1.GND, DS1.GND, DS2.GND
  VIN: U1.Vin, hc-sr1.VCC
  N4: hc-sr1.Echo, R5.Pin_1

notes:
  If you find a 3.3v HC-SR04 then you should be able to use 3.3V instead of 5V for it's VCC and then wire Echo directly to 3.3V input pin D2 and eliminate the two resistors below bing used to drop voltage from 5V to ~3.3V. (Keep the pull up resistor for the Dallas Temperature sensors though!).

custom parts:
  NodeMCU V1.0: ESP8266 based NodeMCU
